# Fritzing sketch Untitled Sketch 2 (saved by Fritzing 0.9.3b)
breadboards: 1

parts:
  Raspberry_Pi_1 = Raspberry Pi 3 [part_number=RPI-3-V1.2]
  Part1 = Monster Moto Shield
  Part2 = Monster Moto Shield
  M1 = DC Motor
  M2 = DC Motor
  M3 = DC Motor
  M4 = DC Motor
  J1 = Basic Servo  # not connected
  D1 = SOLAR-IXYS [package=solarbit-12x1]
  VCC1 = Battery block 9V  # not connected
  BAT1 = BC9VPC [package=bc9vpc]
  BAT2 = BC9VPC [package=bc9vpc]
  IC1 = MICROCONTROLLER [package=dil28-3-simon]

nets:
  N1: Raspberry_Pi_1.5V, IC1.PC6(_RESET), IC1.PC5(ADC5_SCL)
  N2: Part1.OUTA1, M4.pin_1
  N3: Part1.OUTB1, M4.pin_2
  N4: Part1.OUTA2, M1.pin_2
  N5: Part1.OUTB2, M1.pin_1
  N6: Part1.VCC, BAT2.V+
  N7: Part1.GND, BAT2.V-
  N8: Part2.OUTA1, M3.pin_1
  N9: Part2.OUTB1, M3.pin_2
  N10: Part2.OUTA2, M2.pin_2
  N11: Part2.OUTB2, M2.pin_1
  N12: Part2.VCC, BAT1.V+
  N13: Part2.GND, BAT1.V-
  N14: D1.C, IC1.PD4(XCK_T0), IC1.PC0(ADC0)
  N15: IC1.PD0(RXD), IC1.PC4(ADC4_SDA)
  N16: IC1.PD1(TXD), IC1.PC3(ADC3)
  N17: IC1.PD2(INT0), IC1.PC2(ADC2)
  N18: IC1.PD3(INT1), IC1.PC1(ADC1)
  N19: IC1.VCC, IC1.AGND
  N20: IC1.GND, IC1.AREF
  N21: IC1.PB6(XTAL1_TOSC1), IC1.AVCC
  N22: IC1.PB7(XTAL2_TOSC2), IC1.PB5(SCK)
  N23: IC1.PD5(T1), IC1.PB4(MISO)
  N24: IC1.PD6(AIN0), IC1.PB3(MOSI_OC2)
  N25: IC1.PD7(AIN1), IC1.PB2(SS_OC1B)
  N26: IC1.PB0(ICP), IC1.PB1(OC1A)
